# Fritzing sketch heart_rate_system (saved by Fritzing 0.9.3b)
breadboards: 1

parts:
  IC1 = AD8232 HeartRate Monitor [part_number=SEN-12650 chip_label=IC package="DIP (Dual Inline) [THT]"]
  R1 = Resistor [tolerance=±5% resistance=220 package=THT]
  LED1 = LED - 5mm [color="Red (633nm)" package="5 mm [THT]"]
  부품1 = Arduino Uno (Rev3)
  J1 = Piezo Speaker

nets:
  GND: IC1.GND, LED1.cathode, 부품1.GND, J1.pin1
  3.3V: IC1.3.3v, 부품1.3V3
  N1: IC1.OUTPUT, 부품1.A0
  N2: IC1.LO-, 부품1.D11_PWM/MOSI
  N3: IC1.LO+, 부품1.D10_PWM/SS
  N4: R1.Pin_0, LED1.anode
  N5: R1.Pin_1, 부품1.D8
  N6: 부품1.D9_PWM, J1.pin2

custom parts:
  AD8232 HeartRate Monitor: A DIP stand-in part for whatever IC you want. With 10 pins on a 600mil dual inline package (DIP) footprint.
